# Fritzing sketch wakeuplight (saved by Fritzing 0.9.2b)
breadboards: 1

parts:
  Main_Controller = Arduino Nano (Rev3.0)
  230V_Plug = Power plug
  Controls_IO_Expander = PCF8574 [package="DIP16 [THT]"]
  Radio_Module = IC, DIP package, 10 pins [chip_label=RDA5807M]
  RTC_Module = IC, DIP package, 6 pins [chip_label=DS3231]
  230V_AC_Adapter_5V = IC, DIP package, 4 pins [chip_label="AC Adapter"]
  230V_AC_Adapter_12V = IC, DIP package, 4 pins [chip_label="AC Adapter"]
  15W_Amplifier = IC, DIP package, 12 pins [chip_label=PAM8610]
  Darlington_Transistor_(TIP120) = NPN-Transistor [package="TO92 [THT]"]
  part = NPN-Transistor [package="TO92 [THT]"]
  R2 = Resistor [tolerance=±5% resistance=1k package="0603 [SMD]"]
  WS2812B_Ring = IC, SIP package, 4 pins [chip_label="12x WS2812B"]
  10W_Warm_White_LED = LEDs [package=led10mm]
  R3 = Resistor [tolerance=±5% resistance=47 package="0603 [SMD]"]
  R4 = Resistor [tolerance=±5% resistance=22 package="0603 [SMD]"]
  Left_Speaker = SPEAKER [package=pcb_mount_speaker]
  Right_Speaker = SPEAKER [package=pcb_mount_speaker]
  4_Digit_Display = IC, DIP package, 4 pins [chip_label=TM1637]
  L = SWITCH-MOMENTARY-2 [package=tactile-pth-12mm]
  R = SWITCH-MOMENTARY-2 [package=tactile-pth-12mm]
  V+ = SWITCH-MOMENTARY-2 [package=tactile-pth-12mm]
  V- = SWITCH-MOMENTARY-2 [package=tactile-pth-12mm]
  C+ = SWITCH-MOMENTARY-2 [package=tactile-pth-12mm]
  L+ = SWITCH-MOMENTARY-2 [package=tactile-pth-12mm]
  L- = SWITCH-MOMENTARY-2 [package=tactile-pth-12mm]
  C- = SWITCH-MOMENTARY-2 [package=tactile-pth-12mm]
  LDR = Photocell (LDR) [package=THT]
  R5 = Resistor [tolerance=±5% resistance=1k package="0603 [SMD]"]
  + = SWITCH-MOMENTARY-2 [package=tactile-pth-12mm]
  S = SWITCH-MOMENTARY-2 [package=tactile-pth-12mm]
  - = SWITCH-MOMENTARY-2 [package=tactile-pth-12mm]
  A1 = SWITCH-MOMENTARY-2 [package=tactile-pth-12mm]
  A2 = SWITCH-MOMENTARY-2 [package=tactile-pth-12mm]

nets:
  GND: Main_Controller.GND, Controls_IO_Expander.A0, Controls_IO_Expander.A1, Controls_IO_Expander.A3, Controls_IO_Expander.GND, Radio_Module.pin6, RTC_Module.pin6, 230V_AC_Adapter_5V.pin4, 230V_AC_Adapter_12V.pin4, 15W_Amplifier.pin2, 15W_Amplifier.pin8, WS2812B_Ring.pin4, 10W_Warm_White_LED.C, 4_Digit_Display.pin4, L.1, R.1, V+.1, V-.1, C+.1, L+.1, L-.1, C-.1, R5.Pin_1, +.1, S.1, -.1, A1.1, A2.1
  N1: Main_Controller.D3, WS2812B_Ring.pin1
  N2: Main_Controller.D5, R2.Pin_1
  N3: Main_Controller.D6, +.2
  N4: Main_Controller.D7, -.2
  N5: Main_Controller.D8, S.2
  N6: Main_Controller.D9, A1.2
  N7: Main_Controller.D10, A2.2
  N8: Main_Controller.D12/MISO, 4_Digit_Display.pin2
  N9: Main_Controller.VIN, 230V_AC_Adapter_5V.pin3, WS2812B_Ring.pin3, 4_Digit_Display.pin3, LDR.pin_0
  N10: Main_Controller.A5, Controls_IO_Expander.SCL, Radio_Module.pin2, RTC_Module.pin2
  N11: Main_Controller.A4, Controls_IO_Expander.SDA, Radio_Module.pin1, RTC_Module.pin1
  N12: Main_Controller.A0, LDR.pin_1, R5.Pin_0
  N13: Main_Controller.D13/SCK, 4_Digit_Display.pin1
  N14: 230V_Plug.VCC, 230V_AC_Adapter_5V.pin1, 230V_AC_Adapter_12V.pin1
  N15: 230V_Plug.GND, 230V_AC_Adapter_5V.pin2, 230V_AC_Adapter_12V.pin2
  N16: Controls_IO_Expander.P0, R.2
  N17: Controls_IO_Expander.P1, V+.2
  N18: Controls_IO_Expander.P2, V-.2
  N19: Controls_IO_Expander.P3, C+.2
  N20: Controls_IO_Expander.P4, C-.2
  N21: Controls_IO_Expander.P5, L.2
  N22: Controls_IO_Expander.P6, L+.2
  N23: Controls_IO_Expander.P7, L-.2
  N24: Controls_IO_Expander.VCC, Radio_Module.pin5, RTC_Module.pin5
  N25: Radio_Module.pin7, 15W_Amplifier.pin1
  N26: Radio_Module.pin8, 15W_Amplifier.pin3
  N27: 230V_AC_Adapter_12V.pin3, 15W_Amplifier.pin7, Darlington_Transistor_(TIP120).C, part.C
  N28: 15W_Amplifier.pin9, Left_Speaker.-
  N29: 15W_Amplifier.pin10, Left_Speaker.+
  N30: 15W_Amplifier.pin11, Right_Speaker.-
  N31: 15W_Amplifier.pin12, Right_Speaker.+
  N32: Darlington_Transistor_(TIP120).E, part.B
  N33: Darlington_Transistor_(TIP120).B, R2.Pin_0
  N34: part.E, R3.Pin_0, R4.Pin_0
  N35: 10W_Warm_White_LED.A, R3.Pin_1, R4.Pin_1

notes:
  Red's Wake-Up Light, A custom Wake-Up Light with RGB and radio capabilities, v1.3
